# Fritzing sketch Automated Voice Controlled Appliances (saved by Fritzing 0.9.3b)
circuit board: 8.46667cm x 5.64444cm
breadboards: 1

parts:
  U1 = NodeMCU V1.0
  KY-1 = Keyes Relay [package=THT]
  LED1 = smd LED [color="Red (633nm)" package="1206 [SMD]"]
  R1 = Resistor [tolerance=±5% resistance=220 package="2010 [SMD]"]

nets (from the breadboard view):
  N1: U1.D1, KY-1.signal
  N2: U1.3V3, KY-1.NO
  N3: U1.GND, KY-1.ground, LED1.anode
  N4: U1.Vin, KY-1.power
  N5: KY-1.C, R1.Pin_1
  N6: LED1.cathode, R1.Pin_0

custom parts:
  NodeMCU V1.0: ESP8266 based NodeMCU
  Keyes Relay: The Keyes 5V relay module is suitable for SCM development, home appliance control. It uses a 5V~12V TIL control signal which can control DC / AC signal.

// code stored in the sketch: Automated Voice Controlled Appliances.ino
#define WIFI_NAME "GEARBOX STAFF"
#define WIFI_PASSWORD "Staff@Gearbox"
#define DEVICE_ID 2
#define DEVICE_NAME "Google_ESP"
#define TOKEN "~1005414_T1rxsp5LTq1icC94eu1WVEGW"
#define Relay_1 5 

#include <RemoteMe.h>
#include <RemoteMeSocketConnector.h>
#include <RemoteMeDirectWebSocketConnector.h> // !important library needs WebSockets by Markus Sattler Please install it from Library manager

#include <ESP8266WiFi.h>



RemoteMe& remoteMe = RemoteMe::getInstance(TOKEN, DEVICE_ID);

//*************** CODE FOR COMFORTABLE VARIABLE SET *********************

inline void setRelay(boolean b) {remoteMe.getVariables()->setBoolean("Relay", b); }

//*************** IMPLEMENT FUNCTIONS BELOW *********************

void onRelayChange(boolean b) {
	Serial.printf("onRelayChange: b: %d\n",b);
  digitalWrite(Relay_1, b ? HIGH : LOW);
}




void setup() {
	Serial.begin(115200);
  pinMode(Relay_1, OUTPUT);
  digitalWrite(Relay_1, LOW);

	WiFi.begin(WIFI_NAME, WIFI_PASSWORD);

	while (WiFi.status() != WL_CONNECTED) {
		delay(100);
	}

	remoteMe.getVariables()->observeBoolean("Relay" ,onRelayChange);

	remoteMe.setConnector(new RemoteMeSocketConnector());
	remoteMe.setDirectConnector(new RemoteMeDirectWebSocketConnector());
	remoteMe.sendRegisterDeviceMessage(DEVICE_NAME);
}


void loop() {
	remoteMe.loop();
}
